# Fritzing sketch Arduino_Receiver_Buzzer (saved by Fritzing 0.9.2b)

parts:
  NRF24L1 = NRF24L01
  Componente1 = Arduino Uno (Rev3) - ICSP
  Grove1 = Grove Buzz

nets:
  VCC: NRF24L1.VCC, Componente1.3V3
  N1: NRF24L1.CSN, Componente1.D8
  N2: NRF24L1.MOSI, Componente1.ICSP_MOSI, Componente1.D11_PWM/MOSI
  GND: NRF24L1.GND, Componente1.GND, Grove1.GND
  N3: NRF24L1.CE, Componente1.D7
  N4: NRF24L1.SCK, Componente1.D13/SCK
  N5: NRF24L1.MISO, Componente1.ICSP_MISO, Componente1.D12/MISO
  N6: Componente1.D3_PWM, Grove1.SIG
  5V: Componente1.5V, Grove1.VCC

custom parts:
  NRF24L01: NRF24L01 module
